# Fritzing sketch Untitled Sketch 2 (saved by Fritzing 0.9.10b)
breadboards: 1

parts:
  R1 = Resistor [tolerance=±5% power=0.25 resistance=5 package=THT]
  R2 = Resistor [tolerance=±5% power=0.25 resistance=15 package=THT]
  R3 = Resistor [tolerance=±5% power=0.25 resistance=20 package=THT]
  R4 = Resistor [tolerance=±5% power=0.25 resistance=10 package=THT]
  C1 = Ceramic Capacitor [capacitance=0.5mF voltage=35V package="100 mil [THT, multilayer]"]
  S2 = Square Pushbutton
  VCC1 = Battery block 9V
  VCC2 = 4 x AAA Battery Mount

nets:
  N1: R1.Pin_0, VCC2.+
  N2: R1.Pin_1, S2.leg0
  N3: R2.Pin_0, R3.Pin_1, C1.0, VCC1.-
  N4: R2.Pin_1, S2.leg1
  N5: R3.Pin_0, R4.Pin_1
  N6: R4.Pin_0, C1.1
  N7: VCC1.+, VCC2.-
